# Fritzing sketch wiring (saved by Fritzing 0.9.3b)

parts:
  Part1 = Adafruit PyPortal - CircuitPython Powered Internet Display [part_number="Adafruit #4116"]
  SP1 = SPEAKER [package=pcb_mount_speaker]  # not connected
  BUTTON1 = Arcade Button (white)
  Part2 = Adafruit PowerBoost 1000C [part_number="Adafruit #2465"]
  J1 = Power Jack [package=power_jack_pth]
  X1 = USB Connectors [package=usb-a-pcb]

nets:
  N1: Part1.GND, BUTTON1.no_name_yet#1
  N2: Part1.VCC, BUTTON1.no_name_yet#2
  N3: Part1.D3, Part2.5.0V, X1.VBUS
  N4: Part2.VBUS, J1.PWR
  GND: Part2.GND, J1.GND, X1.GND

custom parts:
  Adafruit PyPortal - CircuitPython Powered Internet Display: PyPortal, our upcoming easy-to-use IoT device that allows you to create all the things for the “Internet of Things” in minutes. Make custom touch screen interface GUIs, all open-source, and Python-powered using tinyJSON / APIs to get news, stock, weather, cat photos, and more – all over Wi-Fi with the latest technologies. Create little pocket universes of joy that connect to something good.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
  Arcade Button (white): Adafruit Arcade Button (white)
  Adafruit PowerBoost 1000C: PowerBoost 1000C is the perfect power supply for your portable project! With a built-in load-sharing battery charger circuit, you'll be able to keep your power-hungry project running even while recharging the battery! This little DC/DC boost converter module can be powered by any 3.7V LiIon/LiPoly battery, and convert the battery output to 5.2V DC for running your 5V projects.
